# Fritzing sketch ArduTracker_esp32 (saved by Fritzing 0.9.4)

parts:
  microSD1 = MicroSD Card Module
  Part1 = NRF24L01
  U1 = ESP32S-HiLetgo [part_number=ESP32S-HiLetgo]
  R1 = Resistor [tolerance=±5% resistance=330k package="0805 [SMD]"]

nets:
  GND: microSD1.GND, Part1.GND, U1.GND
  VCC: microSD1.VCC, U1.VIN
  N1: microSD1.MISO, R1.Pin_1
  N2: microSD1.MOSI, Part1.MOSI, U1.GPIO23
  N3: microSD1.SCK, Part1.SCK, U1.GPIO18
  N4: microSD1.CS, U1.GPIO22
  N5: Part1.CSN, U1.GPIO5
  N6: Part1.VCC, U1.3.3
  N7: Part1.MISO, U1.GPIO19, R1.Pin_0
  N8: Part1.CE, U1.GPIO4

notes:
  On the 3.3v SD card cannot be read, use the 5v instaed.
  IMPORTANT: Make sure the red led in the ESP is ON after connecting the power. Otherwise, turn it off immediatly and check the cables or something might start burning.

custom parts:
  ESP32S-HiLetgo: HiLetgo ESP-WROOM-32 ESP32 ESP-32S Development Board 2.4GHz Dual-Mode WiFi + Bluetooth Dual Cores Microcontroller The ESP32 integrated with Antenna switches, RF Balun, power amplifiers, low-noise amplifiers, filters, and management modules, and the entire solution occupies the least area of PCB. 2.4 GHz Wi-Fi plus Bluetooth dual-mode chip, with TSMC Ultra-low power consumption 40nm technology,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
